# Fritzing sketch ESP32 CW Keyer (saved by Fritzing 1.0.8)

parts:
  TRS2 = Audio Jack (TRS) 3.5mm [package="4Ucon 08780 [THT]"]
  A1 = Waveshare esp32-c3-zero tht

nets:
  N1: TRS2.Sleeve, A1.Pin_2
  N2: TRS2.Ring, A1.Pin_9
  N3: TRS2.Tip, A1.Pin_10

custom parts:
  Waveshare esp32-c3-zero tht: ESP32-C3 Mini Development Board, Based on ESP32-C3FN4 Single-core Processor, 160MHz Running Frequency, 2.4GHz Wi-Fi&Bluetooth 5.
